# Fritzing sketch project (saved by Fritzing 0.9.3b)
breadboards: 1

parts:
  Part2 = Arduino Nano (Rev3.0) (ICSP)
  L298N1 = L298N DC motor driver
  BAT1 = 12 battery [package=battery]
  M1 = Getriebemotor
  M2 = Getriebemotor
  M3 = Getriebemotor
  M4 = Getriebemotor
  S1 = KY-026
  S2 = KY-026
  S3 = KY-026
  M5 = 1 chan 5v relay module
  WATER_PUMP1 = water pump/motor  # not connected
  J1 = Dagu DGServo 9g header (male) [package=THT]
  VCC1 = Battery
  M8 = Dagu DGServo 9g (Top view) [part_number=RS001B]
  M9 = Dagu DGServo 9g (Top view) [part_number=RS001B]
  S4 = KY-026

nets:
  GND: Part2.GND, L298N1.GND, BAT1.-, S1.pin2, S2.pin2, S3.pin2, M5.pin_2, M8.gnd, M9.gnd, S4.pin2
  N1: Part2.D2, M9.pulse
  N2: Part2.D3, M8.pulse
  N3: Part2.D6, M5.pin_3
  N4: Part2.D7, L298N1.ENA
  N5: Part2.D8, L298N1.ENB
  N6: Part2.D9, L298N1.IN1
  N7: Part2.D10, L298N1.IN2
  N8: Part2.D11/MOSI, L298N1.IN3
  N9: Part2.D12/MISO, L298N1.IN4
  VIN: Part2.VIN, L298N1.5V
  VCC: Part2.5V, S1.pin3, S2.pin3, S3.pin3, M5.pin_1, M8.vcc, M9.vcc, S4.pin3
  N10: Part2.A3, S4.pin1
  N11: Part2.A2, S3.pin1
  N12: Part2.A1, S2.pin1
  N13: Part2.A0, S1.pin1
  N14: L298N1.OUT1, M1.pin_1, M2.pin_1
  N15: L298N1.OUT2, M1.pin_2, M2.pin_2
  N16: L298N1.OUT3, M3.pin_2, M4.pin_2
  N17: L298N1.OUT4, M3.pin_1, M4.pin_1
  N18: L298N1.12V, BAT1.+
  N19: M5.pin_4, J1.Vcc
  N20: M5.pin_5, VCC1.+
  N21: J1.gnd, VCC1.-

notes:
  Arm robot whit tow joint

custom parts:
  L298N DC motor driver: 2x DC motor driver with 78M05 positive voltage regulator (7..35 V) L298N: max 46 V, 2 A Set 5 V Enable jumper to enable 5 V regultor (needed for the L298N) and +5 V output at screw terminal or supply external +5 V at screw terminal Set ENA and/or ENB to +5 V to enable motor permanently or supply ENA and/or ENB with PWM signal IN1 and IN2 set rotation directory for motor A (OUT1/OUT2) IN2 and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
  12 battery: 12V lead acid type battery, like the Husqvarna YTH2448 12V 35AH battery. This is the mini version 1/4 the size of the actual battery to be closer to typical breadboard parts (around 2in wide rathher than 7in). The pads in pcb are sized to accomidate up to 14ga wire (as these batterys will deliver high currents.)
  KY-026: ky-026 flame sensor module
  1 chan 5v relay module: 1 Channel 5V Relay Module Board Shield with Optocoupler Support High and Low Level Trigger for Arduino.
  water pump/motor: WATER PUMP BY ARDUBLOCKTR
